# Fritzing sketch Hook-up (saved by Fritzing 0.7.12b)
breadboards: 1

parts:
  Arduino1 = Arduino
  Part1 = SRF05 Ultrasonic Rangefinder
  Bluetooth1 = JY-MCU
  IC1 = L293D [package=THT]
  M1 = DC Motor
  M2 = DC Motor
  J1 = Basic Servo
  R1 = Photocell (LDR) [package=THT]
  R2 = Photocell (LDR) [package=THT]
  S1 = Pushbutton [package=THT]
  S2 = Pushbutton [package=THT]
  R3 = Resistor [tolerance=±5% resistance=220 package=THT]
  R4 = Resistor [tolerance=±5% resistance=220 package=THT]

nets:
  N1: Arduino1.D10, IC1.Enable_1
  N2: Arduino1.D9, IC1.Enable_2
  N3: Arduino1.D7, IC1.In_1
  N4: Arduino1.D6, IC1.In_2
  N5: Arduino1.D5, IC1.In_4
  N6: Arduino1.D4, IC1.In_3
  N7: Arduino1.D3, Part1.Echo
  N8: Arduino1.D2, Part1.Trig
  N9: Arduino1.D1TX, Bluetooth1.RX
  N10: Arduino1.D0RX, Bluetooth1.TX
  VCC: Arduino1.+5V, Part1.VCC, J1.vcc, S1.leg0, S2.leg0
  GND: Arduino1.GND, Part1.GND, Bluetooth1.GND, IC1.0V, J1.gnd, R3.Pin_0, R4.Pin_0
  N11: Arduino1.A0, Bluetooth1.VCC, S1.leg1
  N12: Arduino1.A1, R1.pin_0, R2.pin_0, S2.leg1
  N13: Arduino1.A2, R2.pin_1, R4.Pin_1
  N14: Arduino1.A3, R1.pin_1, R3.Pin_1
  N15: IC1.Out_1_(_Controlled_by_Enable_1_), M1.pin_1
  N16: IC1.Out_2_(_Controlled_by_Enable_1_), M1.pin_2
  N17: IC1.+Vmotor, IC1.+V
  N18: IC1.Out_3_(_Controlled_by_Enable_2_), M2.pin_2
  N19: IC1.Out_4_(_Controlled_by_Enable_2_), M2.pin_1

custom parts:
  JY-MCU: Description: The Bluetooth Mate is very similar to our BlueSMiRF modem, but it is designed specifically to be used with our Arduino Pros and LilyPad Arduinos. These modems work as a serial (RX/TX) pipe, and are a great wireless replacement for serial cables. Any serial stream from 9600 to 115200bps can be passed seamlessly from your computer to your target. Bluetooth Mate has the same pin out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
